# Fritzing sketch 7- segment (saved by Fritzing 1.0.5)
breadboards: 1

parts:
  R1 = Resistor [tolerance=±5% power=0.25W resistance=220 package=THT]
  R2 = Resistor [tolerance=±5% power=0.25W resistance=220 package=THT]
  R3 = Resistor [tolerance=±5% power=0.25W resistance=220 package=THT]
  R4 = Resistor [tolerance=±5% power=0.25W resistance=220 package=THT]
  R5 = Resistor [tolerance=±5% power=0.25W resistance=220 package=THT]
  R6 = Resistor [tolerance=±5% power=0.25W resistance=220 package=THT]
  R7 = Resistor [tolerance=±5% power=0.25W resistance=220 package=THT]
  Part1 = Arduino Uno (Rev3)
  DI1 = 7-Segment LED Display [package=THT]

nets:
  N1: R1.Pin_0, Part1.D6_PWM
  N2: R1.Pin_1, DI1.cathodeF
  N3: R2.Pin_0, Part1.D7
  N4: R2.Pin_1, DI1.cathodeG
  N5: R3.Pin_0, DI1.cathodeA
  N6: R3.Pin_1, Part1.D1/TX
  N7: R4.Pin_0, DI1.cathodeB
  N8: R4.Pin_1, Part1.D2
  N9: R5.Pin_0, DI1.cathodeC
  N10: R5.Pin_1, Part1.D3_PWM
  N11: R6.Pin_0, Part1.D4
  N12: R6.Pin_1, DI1.cathodeD
  N13: R7.Pin_0, Part1.D5_PWM
  N14: R7.Pin_1, DI1.cathodeE
  N15: Part1.GND, DI1.commAnode#2
